# Fritzing sketch display (saved by Fritzing 0.9.4)
breadboards: 1

parts:
  U1 = ESP32S-HiLetgo [part_number=ESP32S-HiLetgo]
  IC1 = 2.8 inch LCD SPI display with touch screen & SD card

nets:
  N1: U1.3.3, IC1.pin1, IC1.pin8
  N2: U1.EN, IC1.pin4
  N3: U1.GPIO32, IC1.pin5
  N4: U1.GND, IC1.pin2
  N5: U1.GPIO4, IC1.pin_11
  N6: U1.GPIO5, IC1.pin3
  N7: U1.GPIO18, IC1.pin7, IC1.pin_10
  N8: U1.GPIO19, IC1.pin_9, IC1.pin_13
  N9: U1.GPIO23, IC1.pin6, IC1.pin_12

custom parts:
  ESP32S-HiLetgo: HiLetgo ESP-WROOM-32 ESP32 ESP-32S Development Board 2.4GHz Dual-Mode WiFi + Bluetooth Dual Cores Microcontroller The ESP32 integrated with Antenna switches, RF Balun, power amplifiers, low-noise amplifiers, filters, and management modules, and the entire solution occupies the least area of PCB. 2.4 GHz Wi-Fi plus Bluetooth dual-mode chip, with TSMC Ultra-low power consumption 40nm technology,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
  2.8 inch LCD SPI display with touch screen & SD card: A generic 2.8 inch LCD TFT 320x280 display with touchscreen and SD card slot.
